# Fritzing sketch ESP32ZwiftRider (saved by Fritzing 0.9.4)
breadboards: 1

parts:
  U1 = ESP32S-HiLetgo [part_number=ESP32S-HiLetgo]
  R2 = TRIMPOT [package=3362u-2]
  R3 = TRIMPOT [package=trimpot_pth_s3_lock]

nets:
  N1: U1.3.3, R2.CW, R3.CW
  N2: U1.GND, R2.CCW, R3.CCW

notes:
  RPM: 0 - 120
  WATTS: 0 - 500

custom parts:
  ESP32S-HiLetgo: HiLetgo ESP-WROOM-32 ESP32 ESP-32S Development Board 2.4GHz Dual-Mode WiFi + Bluetooth Dual Cores Microcontroller The ESP32 integrated with Antenna switches, RF Balun, power amplifiers, low-noise amplifiers, filters, and management modules, and the entire solution occupies the least area of PCB. 2.4 GHz Wi-Fi plus Bluetooth dual-mode chip, with TSMC Ultra-low power consumption 40nm technology,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
